// Logisim project EXP_10.circ as structural Verilog: 1 circuit, main circuit main
module main (
  input  C,
  input  B,
  input  A,
  output out_4,
  output out_5
);

  wire AND_1_out, AND_2_out, AND_3_out, OR_1_out, XOR_1_out;

  and AND_1 (AND_1_out, A, B);
  and AND_2 (AND_2_out, A, C);
  and AND_3 (AND_3_out, B, C);
  or OR_1 (OR_1_out, AND_1_out, AND_2_out);
  xor XOR_1 (XOR_1_out, A, B);
  or OR_2 (out_4, OR_1_out, AND_3_out);
  xor XOR_2 (out_5, XOR_1_out, C);

  // Notes on the sheet:
  //   2 BIT FULL ADDER
endmodule
